# Fritzing sketch circa_fritzing (saved by Fritzing 0.9.3b)
perfboards: 1

parts:
  U1 = ESP32S-HiLetgo [part_number=ESP32S-HiLetgo]
  F1 = Fan - Ventilador [package=THT]
  F2 = Fan - Ventilador [package=THT]
  S1 = H-Bridge with L298N
  RGB_SMD_LED1 = SMD RGB LED (WS2812) [package=5050]
  M1 = RioRand LM2596
  L1 = LED - 3mm [color="Yellow (585nm)" package="3 mm [THT]"]
  S5 = Pushbutton [package="[SMD]"]
  RGB_SMD_LED2 = SMD RGB LED (WS2812) [package=5050]  # not connected
  RGB_SMD_LED4 = SMD RGB LED (WS2812) [package=5050]  # not connected
  RGB_SMD_LED5 = SMD RGB LED (WS2812) [package=5050]  # not connected
  RGB_SMD_LED6 = SMD RGB LED (WS2812) [package=5050]  # not connected
  Power_plug1 = Power plug  # not connected

nets:
  N1: U1.GPIO25, S1.IN2
  N2: U1.GPIO26, S1.IN1
  N3: U1.GPIO27, S1.ENA
  N4: U1.GND, L1.anode
  VIN: U1.VIN, S1.5V
  N5: U1.GPIO6, S5.Pin_3, S5.Pin_4
  N6: U1.GPIO8, S5.Pin_1, S5.Pin_2
  N7: U1.GPIO5, S1.ENB
  N8: U1.GPIO18, S1.IN4
  N9: U1.GPIO19, S1.IN3
  N10: F1.5V, S1.M1-02
  N11: F1.GND, S1.M1-01
  N12: F2.5V, S1.M2-02
  N13: F2.GND, S1.M2-01
  N14: S1.12V, M1.Pin_1
  N15: S1.GND, M1.Pin_2
  N16: RGB_SMD_LED1.VCC, M1.Pin_3

notes:
  12V input (dc barrel jack)
  12V in
  5V out, max 4A

custom parts:
  ESP32S-HiLetgo: HiLetgo ESP-WROOM-32 ESP32 ESP-32S Development Board 2.4GHz Dual-Mode WiFi + Bluetooth Dual Cores Microcontroller The ESP32 integrated with Antenna switches, RF Balun, power amplifiers, low-noise amplifiers, filters, and management modules, and the entire solution occupies the least area of PCB. 2.4 GHz Wi-Fi plus Bluetooth dual-mode chip, with TSMC Ultra-low power consumption 40nm technology,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
  Fan - Ventilador: Ventilador de 2 pines, se encuentra comunmente en computadoras de escritorio
  H-Bridge with L298N: h-bridge
